// Logisim project alu.circ as structural Verilog: 4 circuits, main circuit main
module main (
  input  [15:0] a_in,
  input  [15:0] b_in,
  input  [3:0] opcode,
  output [15:0] final_output,
  output error
);

  wire _0_2_out, _0_3_out, _0_out, _1_2_out, _1_3_out, _1_out, _2_2_out, _2_3_out, _2_out, _3_2_out,
       _3_3_out, _3_out, _4_2_out, _4_3_out, _4_out, _5_2_out, _5_3_out, _5_out, _6_2_out, _6_3_out, _6_out,
       _7_2_out, _7_3_out, _7_out, _8_2_out, _8_3_out, _8_out, _9_2_out, _9_3_out, _9_out, adder_1_cout,
       clk_out, n7segment_1_b0, n7segment_1_b1, n7segment_1_b2, n7segment_1_t0, n7segment_1_t1,
       n7segment_1_t2, n7segment_1_t3, n7segment_2_b0, n7segment_2_b1, n7segment_2_b2, n7segment_2_t0,
       n7segment_2_t1, n7segment_2_t2, n7segment_2_t3, n7segment_3_b0, n7segment_3_b1, n7segment_3_b2,
       n7segment_3_t0, n7segment_3_t1, n7segment_3_t2, n7segment_3_t3, n7segment_4_b0, n7segment_4_b1,
       n7segment_4_b2, n7segment_4_t0, n7segment_4_t1, n7segment_4_t2, n7segment_4_t3, n7segment_5_b0,
       n7segment_5_b1, n7segment_5_b2, n7segment_5_t0, n7segment_5_t1, n7segment_5_t2, n7segment_5_t3,
       n7segment_6_b0, n7segment_6_b1, n7segment_6_b2, n7segment_6_t0, n7segment_6_t1, n7segment_6_t2,
       n7segment_6_t3, n7segment_7_b0, n7segment_7_b1, n7segment_7_b2, n7segment_7_t0, n7segment_7_t1,
       n7segment_7_t2, n7segment_7_t3, n7segment_8_b0, n7segment_8_b1, n7segment_8_b2, n7segment_8_t0,
       n7segment_8_t1, n7segment_8_t2, n7segment_8_t3, n7segment_9_b0, n7segment_9_b1, n7segment_9_b2,
       n7segment_9_t0, n7segment_9_t1, n7segment_9_t2, n7segment_9_t3, n7segment_10_b0, n7segment_10_b1,
       n7segment_10_b2, n7segment_10_t0, n7segment_10_t1, n7segment_10_t2, n7segment_10_t3, n7segment_11_b0,
       n7segment_11_b1, n7segment_11_b2, n7segment_11_t0, n7segment_11_t1, n7segment_11_t2, n7segment_11_t3,
       n7segment_12_b0, n7segment_12_b1, n7segment_12_b2, n7segment_12_t0, n7segment_12_t1, n7segment_12_t2,
       n7segment_12_t3, n7segment_13_b0, n7segment_13_b1, n7segment_13_b2, n7segment_13_t0, n7segment_13_t1,
       n7segment_13_t2, n7segment_13_t3, n7segment_14_b0, n7segment_14_b1, n7segment_14_b2, n7segment_14_t0,
       n7segment_14_t1, n7segment_14_t2, n7segment_14_t3, n7segment_15_b0, n7segment_15_b1, n7segment_15_b2,
       n7segment_15_t0, n7segment_15_t1, n7segment_15_t2, n7segment_15_t3, n7segment_16_b0, n7segment_16_b1,
       n7segment_16_b2, n7segment_16_t0, n7segment_16_t1, n7segment_16_t2, n7segment_16_t3, n7segment_17_b0,
       n7segment_17_b1, n7segment_17_b2, n7segment_17_t0, n7segment_17_t1, n7segment_17_t2, n7segment_17_t3,
       nor_1_out, not_1_out, or_1_out, reset_2_out, reset_3_out, reset_4_out, reset_out, subtractor_1_bout;
  wire [3:0] divider_2_rem, divider_3_rem, divider_4_rem, divider_5_rem, divider_6_rem, divider_8_rem,
       divider_9_rem, divider_10_rem, divider_11_rem, divider_12_out, divider_12_rem, divider_15_rem,
       divider_16_rem, divider_17_rem, divider_18_rem, divider_19_rem, numread_3_output, selector_q;
  wire [11:0] numread_3_output_2;
  wire [15:0] a_reg_q, adder_1_out, and_test_out, b_reg_q, bit_extender_1_out, bit_extender_2_out,
       bit_extender_3_out, bit_extender_4_out, bit_extender_5_out, divider_1_rem, divider_3_out,
       divider_4_out, divider_5_out, divider_6_out, divider_7_out, divider_7_rem, divider_8_out,
       divider_9_out, divider_10_out, divider_13_rem, divider_14_out, divider_16_out, divider_17_out,
       divider_18_out, divider_19_out, multiplier_1_cout, multiplier_1_out, nand_test_out, nor_test_out,
       not_test_out, numread_1_output, numread_2_output, or_test_out, pers_op_q, shifter_1_out,
       shifter_2_out, subtractor_1_out, xnor_test_out, xor_test_out;
  wire [15:4] divider_2_rem_2, divider_3_rem_2, divider_4_rem_2, divider_5_rem_2, divider_6_rem_2,
       divider_8_rem_2, divider_9_rem_2, divider_10_rem_2, divider_15_rem_2, divider_16_rem_2,
       divider_17_rem_2, divider_18_rem_2, divider_19_rem_2;

  _7segment u_7segment_1 (
    .Number(divider_1_rem[3:0]), .T2(n7segment_1_t2), .T3(n7segment_1_t3), .B2(n7segment_1_b2),
    .B1(n7segment_1_b1), .B0(n7segment_1_b0), .T1(n7segment_1_t1), .T0(n7segment_1_t0));
  Divider #(.width(16)) divider_1 (.a(divider_3_out), .b(bit_extender_1_out), .rem(divider_1_rem));  // open: out, upper
  _7segment u_7segment_2 (
    .Number(divider_2_rem), .T2(n7segment_2_t2), .T3(n7segment_2_t3), .B2(n7segment_2_b2),
    .B1(n7segment_2_b1), .B0(n7segment_2_b0), .T1(n7segment_2_t1), .T0(n7segment_2_t0));
  Divider #(.width(16)) divider_2 (
    .a(divider_4_out), .b(bit_extender_2_out), .rem({divider_2_rem_2, divider_2_rem}));  // open: out, upper
  _7_Segment_Display u_7_segment_display_1 (
    .g(n7segment_1_t0), .f(n7segment_1_t1), .a(n7segment_1_t2), .b(n7segment_1_t3), .e(n7segment_1_b0),
    .d(n7segment_1_b1), .c(n7segment_1_b2));  // open: dp
  _7_Segment_Display u_7_segment_display_2 (
    .g(n7segment_2_t0), .f(n7segment_2_t1), .a(n7segment_2_t2), .b(n7segment_2_t3), .e(n7segment_2_b0),
    .d(n7segment_2_b1), .c(n7segment_2_b2));  // open: dp
  _7segment u_7segment_3 (
    .Number(divider_3_rem), .T2(n7segment_3_t2), .T3(n7segment_3_t3), .B2(n7segment_3_b2),
    .B1(n7segment_3_b1), .B0(n7segment_3_b0), .T1(n7segment_3_t1), .T0(n7segment_3_t0));
  Divider #(.width(16)) divider_3 (
    .a(divider_5_out), .b(bit_extender_1_out), .out(divider_3_out), .rem({divider_3_rem_2, divider_3_rem}));  // open: upper
  assign bit_extender_1_out = {{12{1'b0}}, 4'b1010};  // Bit_Extender bit_extender_1
  _7segment u_7segment_4 (
    .Number(divider_4_rem), .T2(n7segment_4_t2), .T3(n7segment_4_t3), .B2(n7segment_4_b2),
    .B1(n7segment_4_b1), .B0(n7segment_4_b0), .T1(n7segment_4_t1), .T0(n7segment_4_t0));
  assign bit_extender_2_out = {{12{1'b0}}, 4'b1010};  // Bit_Extender bit_extender_2
  _7_Segment_Display u_7_segment_display_3 (
    .g(n7segment_3_t0), .f(n7segment_3_t1), .a(n7segment_3_t2), .b(n7segment_3_t3), .e(n7segment_3_b0),
    .d(n7segment_3_b1), .c(n7segment_3_b2));  // open: dp
  _7_Segment_Display u_7_segment_display_4 (
    .g(n7segment_4_t0), .f(n7segment_4_t1), .a(n7segment_4_t2), .b(n7segment_4_t3), .e(n7segment_4_b0),
    .d(n7segment_4_b1), .c(n7segment_4_b2));  // open: dp
  Divider #(.width(16)) divider_4 (
    .a(divider_6_out), .b(bit_extender_2_out), .out(divider_4_out), .rem({divider_4_rem_2, divider_4_rem}));  // open: upper
  _7segment u_7segment_5 (
    .Number(divider_5_rem), .T2(n7segment_5_t2), .T3(n7segment_5_t3), .B2(n7segment_5_b2),
    .B1(n7segment_5_b1), .B0(n7segment_5_b0), .T1(n7segment_5_t1), .T0(n7segment_5_t0));
  Divider #(.width(16)) divider_5 (
    .a(divider_7_out), .b(bit_extender_1_out), .out(divider_5_out), .rem({divider_5_rem_2, divider_5_rem}));  // open: upper
  _7segment u_7segment_6 (
    .Number(divider_6_rem), .T2(n7segment_6_t2), .T3(n7segment_6_t3), .B2(n7segment_6_b2),
    .B1(n7segment_6_b1), .B0(n7segment_6_b0), .T1(n7segment_6_t1), .T0(n7segment_6_t0));
  _7_Segment_Display u_7_segment_display_5 (
    .g(n7segment_5_t0), .f(n7segment_5_t1), .a(n7segment_5_t2), .b(n7segment_5_t3), .e(n7segment_5_b0),
    .d(n7segment_5_b1), .c(n7segment_5_b2));  // open: dp
  _7_Segment_Display u_7_segment_display_6 (
    .g(n7segment_6_t0), .f(n7segment_6_t1), .a(n7segment_6_t2), .b(n7segment_6_t3), .e(n7segment_6_b0),
    .d(n7segment_6_b1), .c(n7segment_6_b2));  // open: dp
  Divider #(.width(16)) divider_6 (
    .a(divider_8_out), .b(bit_extender_2_out), .out(divider_6_out), .rem({divider_6_rem_2, divider_6_rem}));  // open: upper
  _7segment u_7segment_7 (
    .Number(divider_7_rem[3:0]), .T2(n7segment_7_t2), .T3(n7segment_7_t3), .B2(n7segment_7_b2),
    .B1(n7segment_7_b1), .B0(n7segment_7_b0), .T1(n7segment_7_t1), .T0(n7segment_7_t0));
  Divider #(.width(16)) divider_7 (
    .a(divider_9_out), .b(bit_extender_1_out), .out(divider_7_out), .rem(divider_7_rem));  // open: upper
  _7_Segment_Display u_7_segment_display_7 (
    .g(n7segment_7_t0), .f(n7segment_7_t1), .a(n7segment_7_t2), .b(n7segment_7_t3), .e(n7segment_7_b0),
    .d(n7segment_7_b1), .c(n7segment_7_b2));  // open: dp
  _7segment u_7segment_8 (
    .Number(divider_8_rem), .T2(n7segment_8_t2), .T3(n7segment_8_t3), .B2(n7segment_8_b2),
    .B1(n7segment_8_b1), .B0(n7segment_8_b0), .T1(n7segment_8_t1), .T0(n7segment_8_t0));
  Divider #(.width(16)) divider_8 (
    .a(divider_10_out), .b(bit_extender_2_out), .out(divider_8_out), .rem({divider_8_rem_2, divider_8_rem}));  // open: upper
  _7segment u_7segment_9 (
    .Number(divider_9_rem), .T2(n7segment_9_t2), .T3(n7segment_9_t3), .B2(n7segment_9_b2),
    .B1(n7segment_9_b1), .B0(n7segment_9_b0), .T1(n7segment_9_t1), .T0(n7segment_9_t0));
  _7_Segment_Display u_7_segment_display_8 (
    .g(n7segment_8_t0), .f(n7segment_8_t1), .a(n7segment_8_t2), .b(n7segment_8_t3), .e(n7segment_8_b0),
    .d(n7segment_8_b1), .c(n7segment_8_b2));  // open: dp
  _7_Segment_Display u_7_segment_display_9 (
    .g(n7segment_9_t0), .f(n7segment_9_t1), .a(n7segment_9_t2), .b(n7segment_9_t3), .e(n7segment_9_b0),
    .d(n7segment_9_b1), .c(n7segment_9_b2));  // open: dp
  Divider #(.width(16)) divider_9 (
    .a(numread_1_output), .b(bit_extender_1_out), .out(divider_9_out), .rem({divider_9_rem_2, divider_9_rem}));  // open: upper
  _7segment u_7segment_10 (
    .Number(divider_10_rem), .T2(n7segment_10_t2), .T3(n7segment_10_t3), .B2(n7segment_10_b2),
    .B1(n7segment_10_b1), .B0(n7segment_10_b0), .T1(n7segment_10_t1), .T0(n7segment_10_t0));
  Divider #(.width(16)) divider_10 (
    .a(numread_2_output), .b(bit_extender_2_out), .out(divider_10_out),
    .rem({divider_10_rem_2, divider_10_rem}));  // open: upper
  _7_Segment_Display u_7_segment_display_10 (
    .g(n7segment_10_t0), .f(n7segment_10_t1), .a(n7segment_10_t2), .b(n7segment_10_t3), .e(n7segment_10_b0),
    .d(n7segment_10_b1), .c(n7segment_10_b2));  // open: dp
  Button reset (.out(reset_out));
  numRead numread_1 (
    .reset(reset_2_out), ._9(_9_out), ._6(_6_out), ._3(_3_out), ._8(_8_2_out), ._5(_5_2_out), ._2(_2_2_out),
    ._0(_0_2_out), ._7(_7_out), ._4(_4_out), ._1(_1_out), .\output (numread_1_output));  // open: clock
  Button _9 (.out(_9_out));
  Button _6 (.out(_6_out));
  Button _3 (.out(_3_out));
  Button reset_2 (.out(reset_2_out));
  numRead numread_2 (
    .reset(reset_out), ._9(_9_2_out), ._6(_6_2_out), ._3(_3_2_out), ._8(_8_out), ._5(_5_out), ._2(_2_out),
    ._0(_0_out), ._7(_7_2_out), ._4(_4_2_out), ._1(_1_2_out), .\output (numread_2_output));  // open: clock
  Button _8 (.out(_8_out));
  Button _9_2 (.out(_9_2_out));
  Button _5 (.out(_5_out));
  Button _6_2 (.out(_6_2_out));
  Button _2 (.out(_2_out));
  Button _3_2 (.out(_3_2_out));
  Button _0 (.out(_0_out));
  Button _7 (.out(_7_out));
  Button _8_2 (.out(_8_2_out));
  Button _5_2 (.out(_5_2_out));
  Button _4 (.out(_4_out));
  Button _2_2 (.out(_2_2_out));
  Button _1 (.out(_1_out));
  Button _0_2 (.out(_0_2_out));
  Button _7_2 (.out(_7_2_out));
  Button _4_2 (.out(_4_2_out));
  Button _1_2 (.out(_1_2_out));
  nor nor_1 (nor_1_out, b_reg_q[7], b_reg_q[0], b_reg_q[1], b_reg_q[2], b_reg_q[3], b_reg_q[4], b_reg_q[5], b_reg_q[6], b_reg_q[8], b_reg_q[9], b_reg_q[10], b_reg_q[11], b_reg_q[12], b_reg_q[13], b_reg_q[14], b_reg_q[15]);
  _7segment u_7segment_11 (
    .Number(divider_11_rem), .T2(n7segment_11_t2), .T3(n7segment_11_t3), .B2(n7segment_11_b2),
    .B1(n7segment_11_b1), .B0(n7segment_11_b0), .T1(n7segment_11_t1), .T0(n7segment_11_t0));
  Clock clk (.out(clk_out));
  and reset_3 (reset_3_out, selector_q[0], selector_q[1], selector_q[3], selector_q[2]);
  assign bit_extender_3_out = {{15{1'b0}}, 1'b0};  // Bit_Extender bit_extender_3
  _7_Segment_Display u_7_segment_display_11 (
    .g(n7segment_11_t0), .f(n7segment_11_t1), .a(n7segment_11_t2), .b(n7segment_11_t3), .e(n7segment_11_b0),
    .d(n7segment_11_b1), .c(n7segment_11_b2));  // open: dp
  Divider #(.width(4)) divider_11 (.a(divider_12_out), .b(4'b1010), .rem(divider_11_rem));  // open: out, upper
  _7segment u_7segment_12 (
    .Number(divider_12_rem), .T2(n7segment_12_t2), .T3(n7segment_12_t3), .B2(n7segment_12_b2),
    .B1(n7segment_12_b1), .B0(n7segment_12_b0), .T1(n7segment_12_t1), .T0(n7segment_12_t0));
  Register #(.width(16)) a_reg (.D(numread_1_output), .Q(a_reg_q), .clk(clk_out), .clr(reset_3_out));  // open: en
  Register #(.width(16)) b_reg (.D(numread_2_output), .Q(b_reg_q), .clk(clk_out), .clr(reset_3_out));  // open: en
  Register #(.width(4)) selector (.D(numread_3_output), .Q(selector_q), .clk(clk_out), .clr(1'b0));  // open: en
  _7_Segment_Display u_7_segment_display_12 (
    .g(n7segment_12_t0), .f(n7segment_12_t1), .a(n7segment_12_t2), .b(n7segment_12_t3), .e(n7segment_12_b0),
    .d(n7segment_12_b1), .c(n7segment_12_b2));  // open: dp
  Divider #(.width(4)) divider_12 (
    .a(numread_3_output), .b(4'b1010), .out(divider_12_out), .rem(divider_12_rem));  // open: upper
  assign and_test_out = a_reg_q & b_reg_q;  // AND_Gate and_test, 16 bits wide
  assign or_test_out = a_reg_q | b_reg_q;  // OR_Gate or_test, 16 bits wide
  assign xor_test_out = a_reg_q ^ b_reg_q;  // XOR_Gate xor_test, 16 bits wide
  Adder #(.width(16)) adder_1 (.a(a_reg_q), .b(b_reg_q), .out(adder_1_out), .cin(1'b0), .cout(adder_1_cout));
  Multiplier #(.width(16)) multiplier_1 (
    .a(a_reg_q), .b(b_reg_q), .out(multiplier_1_out), .cin(bit_extender_3_out), .cout(multiplier_1_cout));
  Divider #(.width(16)) divider_13 (.a(a_reg_q), .b(b_reg_q), .rem(divider_13_rem));  // open: out, upper
  Button reset_4 (.out(reset_4_out));
  Shifter #(.width(16), .shift("lr")) shifter_1 (.in(a_reg_q), .\dist (b_reg_q[3:0]), .out(shifter_1_out));
  assign not_test_out = ~a_reg_q;  // NOT_Gate not_test, 16 bits wide
  assign nand_test_out = ~(a_reg_q & b_reg_q);  // NAND_Gate nand_test, 16 bits wide
  assign nor_test_out = ~(a_reg_q | b_reg_q);  // NOR_Gate nor_test, 16 bits wide
  numRead numread_3 (
    .reset(reset_4_out), ._9(_9_3_out), ._6(_6_3_out), ._3(_3_3_out), ._8(_8_3_out), ._5(_5_3_out),
    ._2(_2_3_out), ._0(_0_3_out), ._7(_7_3_out), ._4(_4_3_out), ._1(_1_3_out),
    .\output ({numread_3_output_2, numread_3_output}));  // open: clock
  Button _8_3 (.out(_8_3_out));
  Button _9_3 (.out(_9_3_out));
  Button _6_3 (.out(_6_3_out));
  Button _5_3 (.out(_5_3_out));
  Button _2_3 (.out(_2_3_out));
  Button _3_3 (.out(_3_3_out));
  Button _0_3 (.out(_0_3_out));
  Button _7_3 (.out(_7_3_out));
  Button _4_3 (.out(_4_3_out));
  Button _1_3 (.out(_1_3_out));
  assign bit_extender_4_out = {{15{1'b0}}, not_1_out};  // Bit_Extender bit_extender_4
  not not_1 (not_1_out, reset_3_out);
  assign xnor_test_out = ~(a_reg_q ^ b_reg_q);  // XNOR_Gate xnor_test, 16 bits wide
  Multiplexer #(.select(4), .width(16), .disabled(0), .enable("false")) multiplexer_1 (
    .in0(pers_op_q), .in1(and_test_out), .in2(or_test_out), .in3(xor_test_out), .in4(adder_1_out),
    .in5(multiplier_1_out), .in6(shifter_1_out), .in7(not_test_out), .in8(divider_13_rem),
    .in9(nand_test_out), .in10(nor_test_out), .in11(xnor_test_out), .in12(subtractor_1_out),
    .in13(divider_14_out), .in14(shifter_2_out), .in15(bit_extender_4_out), .out(final_output),
    .sel(selector_q));
  Subtractor #(.width(16)) subtractor_1 (
    .a(a_reg_q), .b(b_reg_q), .out(subtractor_1_out), .bin(1'b0), .bout(subtractor_1_bout));
  or or_1 (or_1_out, multiplier_1_cout[0], multiplier_1_cout[1], multiplier_1_cout[2], multiplier_1_cout[3], multiplier_1_cout[4], multiplier_1_cout[5], multiplier_1_cout[6], multiplier_1_cout[7], multiplier_1_cout[8], multiplier_1_cout[9], multiplier_1_cout[10], multiplier_1_cout[11], multiplier_1_cout[12], multiplier_1_cout[13], multiplier_1_cout[14], multiplier_1_cout[15]);
  Divider #(.width(16)) divider_14 (.a(a_reg_q), .b(b_reg_q), .out(divider_14_out));  // open: upper, rem
  Register #(.width(16)) pers_op (.D(final_output), .Q(pers_op_q), .clk(clk_out), .clr(reset_3_out));  // open: en
  Shifter #(.width(16)) shifter_2 (.in(a_reg_q), .\dist (b_reg_q[3:0]), .out(shifter_2_out));
  Multiplexer #(.select(4), .disabled(0), .enable("false")) multiplexer_2 (
    .in0(1'b0), .in1(1'b0), .in2(1'b0), .in3(1'b0), .in4(adder_1_cout), .in5(or_1_out), .in6(1'b0),
    .in7(1'b0), .in8(nor_1_out), .in9(1'b0), .in10(1'b0), .in11(1'b0), .in12(subtractor_1_bout),
    .in13(nor_1_out), .in14(1'b0), .in15(1'b0), .out(error), .sel(selector_q));
  _7segment u_7segment_13 (
    .Number(divider_15_rem), .T2(n7segment_13_t2), .T3(n7segment_13_t3), .B2(n7segment_13_b2),
    .B1(n7segment_13_b1), .B0(n7segment_13_b0), .T1(n7segment_13_t1), .T0(n7segment_13_t0));
  Divider #(.width(16)) divider_15 (
    .a(divider_16_out), .b(bit_extender_5_out), .rem({divider_15_rem_2, divider_15_rem}));  // open: out, upper
  _7_Segment_Display u_7_segment_display_13 (
    .g(n7segment_13_t0), .f(n7segment_13_t1), .a(n7segment_13_t2), .b(n7segment_13_t3), .e(n7segment_13_b0),
    .d(n7segment_13_b1), .c(n7segment_13_b2));  // open: dp
  _7segment u_7segment_14 (
    .Number(divider_16_rem), .T2(n7segment_14_t2), .T3(n7segment_14_t3), .B2(n7segment_14_b2),
    .B1(n7segment_14_b1), .B0(n7segment_14_b0), .T1(n7segment_14_t1), .T0(n7segment_14_t0));
  Divider #(.width(16)) divider_16 (
    .a(divider_17_out), .b(bit_extender_5_out), .out(divider_16_out), .rem({divider_16_rem_2, divider_16_rem}));  // open: upper
  assign bit_extender_5_out = {{12{1'b0}}, 4'b1010};  // Bit_Extender bit_extender_5
  _7_Segment_Display u_7_segment_display_14 (
    .g(n7segment_14_t0), .f(n7segment_14_t1), .a(n7segment_14_t2), .b(n7segment_14_t3), .e(n7segment_14_b0),
    .d(n7segment_14_b1), .c(n7segment_14_b2));  // open: dp
  _7segment u_7segment_15 (
    .Number(divider_17_rem), .T2(n7segment_15_t2), .T3(n7segment_15_t3), .B2(n7segment_15_b2),
    .B1(n7segment_15_b1), .B0(n7segment_15_b0), .T1(n7segment_15_t1), .T0(n7segment_15_t0));
  Divider #(.width(16)) divider_17 (
    .a(divider_18_out), .b(bit_extender_5_out), .out(divider_17_out), .rem({divider_17_rem_2, divider_17_rem}));  // open: upper
  _7_Segment_Display u_7_segment_display_15 (
    .g(n7segment_15_t0), .f(n7segment_15_t1), .a(n7segment_15_t2), .b(n7segment_15_t3), .e(n7segment_15_b0),
    .d(n7segment_15_b1), .c(n7segment_15_b2));  // open: dp
  _7segment u_7segment_16 (
    .Number(divider_18_rem), .T2(n7segment_16_t2), .T3(n7segment_16_t3), .B2(n7segment_16_b2),
    .B1(n7segment_16_b1), .B0(n7segment_16_b0), .T1(n7segment_16_t1), .T0(n7segment_16_t0));
  _7_Segment_Display u_7_segment_display_16 (
    .g(n7segment_16_t0), .f(n7segment_16_t1), .a(n7segment_16_t2), .b(n7segment_16_t3), .e(n7segment_16_b0),
    .d(n7segment_16_b1), .c(n7segment_16_b2));  // open: dp
  Divider #(.width(16)) divider_18 (
    .a(divider_19_out), .b(bit_extender_5_out), .out(divider_18_out), .rem({divider_18_rem_2, divider_18_rem}));  // open: upper
  _7segment u_7segment_17 (
    .Number(divider_19_rem), .T2(n7segment_17_t2), .T3(n7segment_17_t3), .B2(n7segment_17_b2),
    .B1(n7segment_17_b1), .B0(n7segment_17_b0), .T1(n7segment_17_t1), .T0(n7segment_17_t0));
  _7_Segment_Display u_7_segment_display_17 (
    .g(n7segment_17_t0), .f(n7segment_17_t1), .a(n7segment_17_t2), .b(n7segment_17_t3), .e(n7segment_17_b0),
    .d(n7segment_17_b1), .c(n7segment_17_b2));  // open: dp
  Divider #(.width(16)) divider_19 (
    .a(final_output), .b(bit_extender_5_out), .out(divider_19_out), .rem({divider_19_rem_2, divider_19_rem}));  // open: upper

  // Notes on the sheet:
  //   A Input
  //   B Input
  //   Opcode
  //   Test for divide by 0
  //   a
  //   b
  //   SRL
  //   Modulus
  //   out[0] through out[15]
  //   Addition overflow check
  //   Multiplication overflow check
  //   Divide
  //   SLL
  //   Output
endmodule

module _7segment (
  input  [3:0] Number,
  output T2,
  output T3,
  output B2,
  output B1,
  output B0,
  output T1,
  output T0
);

  wire decoder_1_out0, decoder_1_out1, decoder_1_out2, decoder_1_out3, decoder_1_out4, decoder_1_out5,
       decoder_1_out6, decoder_1_out7, decoder_1_out8;

  Decoder #(.select(4)) decoder_1 (
    .out0(decoder_1_out0), .out1(decoder_1_out1), .out2(decoder_1_out2), .out3(decoder_1_out3),
    .out4(decoder_1_out4), .out5(decoder_1_out5), .out6(decoder_1_out6), .out7(decoder_1_out7),
    .out8(decoder_1_out8), .sel(Number));  // open: out9, out10, out11, out12, out13, out14, out15, en
  nor a (T2, decoder_1_out1, decoder_1_out4);
  nor b (T3, decoder_1_out5, decoder_1_out6);
  not c (B2, decoder_1_out2);
  nor d (B1, decoder_1_out1, decoder_1_out4, decoder_1_out7);
  or e (B0, decoder_1_out0, decoder_1_out2, decoder_1_out6, decoder_1_out8);
  nor f (T1, decoder_1_out1, decoder_1_out2, decoder_1_out3, decoder_1_out7);
  nor g (T0, decoder_1_out0, decoder_1_out1, decoder_1_out7);
endmodule

module numpad (
  input  _9,
  input  _8,
  input  _7,
  input  _6,
  input  _5,
  input  _4,
  input  _3,
  input  _2,
  input  _1,
  input  _0,
  output [3:0] \output 
);

  wire or_1_out, or_2_out, or_3_out, or_4_out, or_5_out, or_6_out, or_7_out, or_8_out, or_9_out;

  or or_1 (or_1_out, _9, _8);
  or or_2 (or_2_out, _7, _6, _5, _4);
  or or_3 (or_3_out, _7, _6, _3, _2);
  or or_4 (or_4_out, _9, _7, _5, _3, _1);
  or or_5 (or_5_out, or_1_out, _0);
  or or_6 (or_6_out, or_2_out, _0);
  or or_7 (or_7_out, or_3_out, _0);
  or or_8 (or_8_out, or_4_out, _0);
  or or_9 (or_9_out, or_5_out, or_6_out, or_8_out, or_7_out);
  D_Flip_Flop u__8 (.clk(or_9_out), .D(or_1_out), .Q(\output [3]));  // open: Qn, preset, en, reset
  D_Flip_Flop u__4 (.clk(or_9_out), .D(or_2_out), .Q(\output [2]));  // open: Qn, preset, en, reset
  D_Flip_Flop u__2 (.clk(or_9_out), .D(or_3_out), .Q(\output [1]));  // open: Qn, preset, en, reset
  D_Flip_Flop u__1 (.clk(or_9_out), .D(or_4_out), .Q(\output [0]));  // open: Qn, preset, en, reset
endmodule

module numRead (
  input  clock,
  input  reset,
  input  _9,
  input  _8,
  input  _7,
  input  _6,
  input  _5,
  input  _4,
  input  _3,
  input  _2,
  input  _1,
  input  _0,
  output [15:0] \output 
);

  wire or_1_out;
  wire [3:0] numpad_1_output;
  wire [15:0] adder_1_out, bit_extender_1_out, multiplier_1_out;

  or or_1 (or_1_out, _0, _9, _1, _2, _3, _5, _6, _7, _8, _4);
  numpad numpad_1 (
    .\output (numpad_1_output), ._9(_9), ._6(_6), ._3(_3), ._8(_8), ._5(_5), ._2(_2), ._0(_0), ._7(_7),
    ._4(_4), ._1(_1));
  assign bit_extender_1_out = {{12{1'b0}}, numpad_1_output};  // Bit_Extender bit_extender_1
  Adder #(.width(16)) adder_1 (.a(multiplier_1_out), .b(bit_extender_1_out), .out(adder_1_out));  // open: cin, cout
  Register #(.width(16), .trigger("falling")) register_1 (
    .D(adder_1_out), .Q(\output ), .clk(or_1_out), .clr(reset));  // open: en
  Multiplier #(.width(16)) multiplier_1 (.a(\output ), .b(16'ha), .out(multiplier_1_out));  // open: cin, cout
endmodule
